# Fritzing sketch Button Array (saved by Fritzing 1.0.2b)
breadboards: 2

parts:
  Part1 = Arduino Nano (Rev3.0)
  R1 = Resistor [tolerance=±5% resistance=330 package="2512 [SMD]"]
  R2 = Resistor [tolerance=±5% resistance=330 package="2512 [SMD]"]
  R3 = Resistor [tolerance=±5% resistance=330 package="2512 [SMD]"]
  R4 = Resistor [tolerance=±5% resistance=330 package="2512 [SMD]"]
  R5 = Resistor [tolerance=±5% resistance=330 package="2512 [SMD]"]
  R6 = Resistor [tolerance=±5% resistance=330 package="2512 [SMD]"]
  R7 = Resistor [tolerance=±5% resistance=330 package="2512 [SMD]"]
  R8 = Resistor [tolerance=±5% resistance=330 package="2512 [SMD]"]
  R9 = Resistor [tolerance=±5% resistance=330 package="2512 [SMD]"]
  S1 = Taiway 100-SP-X-T1 SPDT Miniature Toggle Switch [part_number=100-SP-X-T1-0-0-B1-M2 package=THT]
  S2 = Taiway 100-SP-X-T1 SPDT Miniature Toggle Switch [part_number=100-SP-X-T1-0-0-B1-M2 package=THT]
  VCC1 = Battery block 9V

nets:
  N1: Part1.GND, R1.Pin_1, R2.Pin_1, R3.Pin_1, R4.Pin_1, R5.Pin_1, R6.Pin_1, R7.Pin_1, R8.Pin_1, R9.Pin_1, VCC1.-
  N2: Part1.D2, R4.Pin_0, S1.L1
  N3: Part1.D3, R3.Pin_0, S1.L2
  N4: Part1.D4, R1.Pin_0, S2.L1
  N5: Part1.D5, R2.Pin_0, S2.L2
  N6: Part1.D6, R5.Pin_0
  N7: Part1.D7, R6.Pin_0
  N8: Part1.D8, R7.Pin_0
  N9: Part1.D9, R8.Pin_0
  N10: Part1.D10, R9.Pin_0
  N11: Part1.5V, S1.COM
  N12: S2.COM, VCC1.+

// code stored in the sketch: UtilTest_ButtonLedHall_2.1.ino
#include <Arduino.h>
#include "PT_Util.h"

Button powerButton(2, Button::PUSH);
Led statusLamp(10, Led::BLINK, Led::NO);

//Button toggleBrakes(4, Button::PUSH);
Led brakesRed(9, Led::BLINK, Led::NC);
Led brakesGreen(11, Led::BLINK, Led::NC);
Led brakesBlue(12, Led::BLINK, Led::NC);

//Timer lampBlink(1000);

int tps = 21;

//unsigned long tempElapsedTime;

void setup() {
  Serial.begin(9600);
  //statusLamp.setLedMode(Led::NO);
  statusLamp.setLedState(Led::BLINK, 250);
  
  brakesRed.setLedState(Led::BLINK, 250);
  brakesGreen.setLedState(Led::BLINK, 250);
  brakesBlue.setLedState(Led::BLINK, 250);
}

void loop() {

  powerButton.controlLed(statusLamp);//, Led::ON, Led::BLINK);
  //statusLamp.update();
  
  brakesRed.update();
  brakesGreen.update();
  brakesBlue.update();
  delay(1000 / tps);
}
