# Fritzing sketch Test1 (saved by Fritzing 1.0.2b)
circuit board: 10cm x 6cm
breadboards: 1

parts:
  Arduino_Nano = Arduino Nano (Rev3.0)
  Transistor_Array = ULN2003A [package="DIP16 [THT]"]
  Shift_Registor = 74HC595 [package="DIP16 [THT]"]  # not connected
  Shift_Register_Breakout = Shift Register Breakout - 74HC595  # not connected
  Multiplexer = 74HC4051 [package=so16]  # not connected
  9V = Battery block 9V  # not connected
  J1 = Camdenboss CTB0158-8 [part_number=CTB0158-8 package=THT]

nets:
  N1: Arduino_Nano.GND, Transistor_Array.0V
  N2: Arduino_Nano.D2, Transistor_Array.In_1
  N3: Arduino_Nano.D3, Transistor_Array.In_2
  N4: Arduino_Nano.D4, Transistor_Array.In_3
  N5: Arduino_Nano.D5, Transistor_Array.In_4
  N6: Arduino_Nano.D6, Transistor_Array.In_5
  N7: Arduino_Nano.D7, Transistor_Array.In_6
  N8: Arduino_Nano.D8, Transistor_Array.In_7
  N9: Transistor_Array.COM_-_Common, J1.pin8
  N10: Transistor_Array.Out_7, J1.pin7
  N11: Transistor_Array.Out_6, J1.pin6
  N12: Transistor_Array.Out_5, J1.pin5
  N13: Transistor_Array.Out_4, J1.pin4
  N14: Transistor_Array.Out_3, J1.pin3
  N15: Transistor_Array.Out_2, J1.pin2
  N16: Transistor_Array.Out_1, J1.pin1
